// Logisim project lab9.circ as structural Verilog: 2 circuits, main circuit main
module main (
  input  Cin,
  input  [3:0] X,
  input  [3:0] Y,
  output [4:0] S
);

  wire full_adder_1_c, full_adder_2_c, full_adder_3_c;

  full_adder full_adder_1 (.X(Y[0]), .Y(X[0]), .Z(Cin), .S(S[0]), .C(full_adder_1_c));
  full_adder full_adder_2 (.X(full_adder_1_c), .Y(Y[1]), .Z(X[1]), .S(S[1]), .C(full_adder_2_c));
  full_adder full_adder_3 (.X(full_adder_2_c), .Y(Y[2]), .Z(X[2]), .S(S[2]), .C(full_adder_3_c));
  full_adder full_adder_4 (.X(full_adder_3_c), .Y(Y[3]), .Z(X[3]), .S(S[3]), .C(S[4]));
endmodule

module full_adder (
  input  X,
  input  Y,
  input  Z,
  output S,
  output C
);

  wire and_1_out, and_2_out, xor_1_out;

  xor xor_1 (xor_1_out, X, Y);
  and and_1 (and_1_out, X, Y);
  xor xor_2 (S, xor_1_out, Z);
  and and_2 (and_2_out, xor_1_out, Z);
  or or_1 (C, and_2_out, and_1_out);
endmodule
